# Fritzing sketch temp_transmitter (saved by Fritzing 0.9.0b)
breadboards: 1

parts:
  RHT1 = Humidity and Temperature Sensor RHT03
  R1 = Resistor [tolerance=±5% resistance=220 package=THT]
  U1 = RF-LINK_TX [package=rf-link_tx]
  Part1 = Arduino Uno (Rev3)

nets:
  VCC: RHT1.Vcc, R1.Pin_0, U1.+5V, Part1.5V
  N1: RHT1.Data-signal, R1.Pin_1, Part1.D4
  GND: RHT1.GND_2, U1.GND, Part1.GND
  N2: U1.DATA, Part1.D3_PWM
