# Fritzing sketch transmitter (saved by Fritzing 0.9.0b)
breadboards: 1

parts:
  Part1 = Arduino Uno (Rev3)
  U1 = RF-LINK_TX [package=rf-link_tx]
  RHT1 = Humidity and Temperature Sensor RHT03
  R1 = Resistor [tolerance=±5% resistance=220 package=THT]

nets:
  N1: Part1.D3_PWM, U1.DATA
  N2: Part1.D4, RHT1.Data-signal, R1.Pin_0
  5V: Part1.5V, U1.+5V, RHT1.Vcc, R1.Pin_1
  GND: Part1.GND, U1.GND, RHT1.GND_2

notes:
  Antenna
